// Logisim project ALU.circ as structural Verilog: 1 circuit, main circuit main
module main (
  input  in_1,
  input  in_2,
  input  in_3,
  input  in_4,
  input  in_5,
  input  in_6,
  input  in_7,
  input  in_8,
  input  in_9,
  input  in_10,
  input  in_11,
  input  in_12,
  input  in_13
);

  NOT_main main_1 (.in_1(in_1), .in_2(in_1), .in_3(in_3), .in_4(in_4));  // open: out_5, out_6, out_7, out_8
  _4_Bit_A_S_main main_2 (
    .in_1(in_1), .in_2(in_2), .in_3(in_3), .in_4(in_5), .in_5(in_4), .in_6(in_6), .in_7(in_7), .in_8(in_9),
    .in_9(in_8));  // open: out_10, out_11, out_12, out_13, out_14
  _16_1_MUX_main main_3 (
    .in_17(in_10), .in_18(in_11), .in_19(in_12), .in_20(in_13));  // open: in_1, in_2, in_3, in_4, in_5, in_6, in_7, in_8, in_9, in_10, in_11, in_12, in_13, in_14, in_15, in_16, out_21
  AND_main main_4 (
    .in_1(in_1), .in_2(in_5), .in_3(in_2), .in_4(in_6), .in_5(in_3), .in_6(in_7), .in_7(in_4), .in_8(in_8));  // open: out_9, out_10, out_11, out_12
  NAND_main main_5 (
    .in_1(in_1), .in_2(in_5), .in_3(in_2), .in_4(in_6), .in_5(in_3), .in_6(in_7), .in_7(in_4), .in_8(in_7));  // open: out_9, out_10, out_11, out_12
  _16_1_MUX_main main_6 (
    .in_17(in_10), .in_18(in_11), .in_19(in_12), .in_20(in_13));  // open: in_1, in_2, in_3, in_4, in_5, in_6, in_7, in_8, in_9, in_10, in_11, in_12, in_13, in_14, in_15, in_16, out_21
  OR_main main_7 (
    .in_1(in_1), .in_2(in_5), .in_3(in_2), .in_4(in_6), .in_5(in_3), .in_6(in_7), .in_7(in_4), .in_8(in_8));  // open: out_9, out_10, out_11, out_12
  _16_1_MUX_main main_8 (
    .in_17(in_10), .in_18(in_11), .in_19(in_12), .in_20(in_13));  // open: in_1, in_2, in_3, in_4, in_5, in_6, in_7, in_8, in_9, in_10, in_11, in_12, in_13, in_14, in_15, in_16, out_21
  NOR_main main_9 (
    .in_1(in_1), .in_2(in_5), .in_3(in_2), .in_4(in_6), .in_5(in_3), .in_6(in_7), .in_7(in_4), .in_8(in_8));  // open: out_9, out_10, out_11, out_12
  XOR_main main_10 (
    .in_1(in_1), .in_2(in_5), .in_3(in_2), .in_4(in_6), .in_5(in_3), .in_6(in_7), .in_7(in_4), .in_8(in_7));  // open: out_9, out_10, out_11, out_12
  XNOR_main main_11 (
    .in_1(in_1), .in_2(in_5), .in_3(in_2), .in_4(in_6), .in_5(in_3), .in_6(in_7), .in_7(in_4), .in_8(in_8));  // open: out_9, out_10, out_11, out_12
  _16_1_MUX_main main_12 (
    .in_17(in_10), .in_18(in_11), .in_19(in_12), .in_20(in_13));  // open: in_1, in_2, in_3, in_4, in_5, in_6, in_7, in_8, in_9, in_10, in_11, in_12, in_13, in_14, in_15, in_16, out_21

  // Notes on the sheet:
  //   Comparision
  //   Shifting
  //   counter
  //   floating point
endmodule
