// Logisim project 4 Bit A S.circ as structural Verilog: 1 circuit, main circuit main
module main (
  input  in_1,
  input  in_2,
  input  in_3,
  input  in_4,
  input  in_5,
  input  in_6,
  input  in_7,
  input  in_8,
  input  in_9,
  output out_10,
  output out_11,
  output out_12,
  output out_13,
  output out_14
);

  wire main_1_out_14, xor_1_out, xor_2_out, xor_3_out, xor_4_out;

  xor xor_1 (xor_1_out, in_4, in_8);
  xor xor_2 (xor_2_out, in_6, in_8);
  xor xor_3 (xor_3_out, in_7, in_8);
  xor xor_4 (xor_4_out, in_9, in_8);
  _4_Bit_Adder_main main_1 (
    .in_1(in_5), .in_2(xor_4_out), .in_3(in_8), .in_4(in_3), .in_5(xor_3_out), .in_6(in_2), .in_7(xor_2_out),
    .in_8(in_1), .in_9(xor_1_out), .out_10(out_13), .out_11(out_12), .out_12(out_11), .out_13(out_10),
    .out_14(main_1_out_14));
  xor xor_5 (out_14, main_1_out_14, in_8);
endmodule
