// Logisim project 4 Bit Adder.circ as structural Verilog: 1 circuit, main circuit main
module main (
  input  in_1,
  input  in_2,
  input  in_3,
  input  in_4,
  input  in_5,
  input  in_6,
  input  in_7,
  input  in_8,
  input  in_9,
  output out_10,
  output out_11,
  output out_12,
  output out_13,
  output out_14
);

  wire main_1_out_5, main_2_out_5, main_3_out_5;

  Full_Adder_main main_1 (.in_1(in_1), .in_2(in_2), .in_3(in_3), .out_4(out_10), .out_5(main_1_out_5));
  Full_Adder_main main_2 (.in_1(in_4), .in_2(in_5), .in_3(main_1_out_5), .out_4(out_11), .out_5(main_2_out_5));
  Full_Adder_main main_3 (.in_1(in_6), .in_2(in_7), .in_3(main_2_out_5), .out_4(out_12), .out_5(main_3_out_5));
  Full_Adder_main main_4 (.in_1(in_8), .in_2(in_9), .in_3(main_3_out_5), .out_4(out_13), .out_5(out_14));
endmodule
