// Logisim project Full Adder.circ as structural Verilog: 1 circuit, main circuit main
module main (
  input  in_1,
  input  in_2,
  input  in_3,
  output out_4,
  output out_5
);

  wire main_1_out_3, main_1_out_4, main_2_out_4;

  Half_Adder_main main_1 (.in_1(in_1), .in_2(in_2), .out_3(main_1_out_3), .out_4(main_1_out_4));
  Half_Adder_main main_2 (.in_1(main_1_out_3), .in_2(in_3), .out_3(out_4), .out_4(main_2_out_4));
  or or_1 (out_5, main_2_out_4, main_1_out_4);
endmodule
