// Logisim project 16 1 MUX.circ as structural Verilog: 1 circuit, main circuit main
module main (
  input  in_1,
  input  in_2,
  input  in_3,
  input  in_4,
  input  in_5,
  input  in_6,
  input  in_7,
  input  in_8,
  input  in_9,
  input  in_10,
  input  in_11,
  input  in_12,
  input  in_13,
  input  in_14,
  input  in_15,
  input  in_16,
  input  in_17,
  input  in_18,
  input  in_19,
  input  in_20,
  output out_21
);

  wire main_1_out_12, main_2_out_12;

  _8_1_MUX_main main_1 (
    .in_1(in_1), .in_2(in_2), .in_3(in_3), .in_4(in_4), .in_5(in_5), .in_6(in_6), .in_7(in_7), .in_8(in_8),
    .out_12(main_1_out_12), .in_9(in_17), .in_10(in_18), .in_11(in_19));
  _8_1_MUX_main main_2 (
    .in_1(in_9), .in_2(in_10), .in_3(in_11), .in_4(in_12), .in_5(in_13), .in_6(in_14), .in_7(in_15),
    .in_8(in_16), .out_12(main_2_out_12), .in_9(in_17), .in_10(in_18), .in_11(in_19));
  Multiplexer #(.enable("false")) multiplexer_1 (.in0(main_1_out_12), .in1(main_2_out_12), .out(out_21), .sel(in_20));
endmodule
